# Fritzing sketch Circuito MagicBox (saved by Fritzing 0.9.3b)
breadboards: 1

parts:
  Componente1 = Arduino Uno (Rev3)
  Componente2 = SRF05 Ultrasonic Rangefinder
  Componente3 = SRF05 Ultrasonic Rangefinder
  Componente4 = SRF05 Ultrasonic Rangefinder
  Componente5 = Bluetooth HC-05 Macho
  Componente6 = HX711 Weighing Sensor Module
  Load_Cell1 = Load Cell - Red/white/black/green
  Part1 = KY-006 Passive Buzzer Module [package="Breakout board"]
  S1 = SWITCH-MOMENTARY-2 [package=tactile_switch_smd-2]
  F1 = Fan - Ventilador [package=THT]  # not connected
  F2 = Fan - Ventilador [package=THT]
  J1 = Peltier Element
  J2 = ATX24 Pin Power Supply Connector [package=atx24_right_angle]
  DS2 = DS18B20 1-Wire Temperature Sensor Probe Cable
  KY-1 = Keyes Relay [package=THT]
  KY-2 = Keyes Relay [package=THT]
  KY-3 = Keyes Relay [package=THT]
  KY-4 = Keyes Relay [package=THT]
  U1 = WS2812 RGB LED matrix 1x8

nets:
  N1: Componente1.A0, Componente6.DO/RX
  N2: Componente1.A1, Componente6.CK/TX
  N3: Componente1.A2, KY-2.signal
  N4: Componente1.A3, KY-3.signal, KY-3.power
  N5: Componente1.A4/SDA, KY-4.signal
  N6: Componente1.D8, Componente5.RXD
  N7: Componente1.D9_PWM, Componente4.Echo
  N8: Componente1.D10_PWM/SS, Componente3.Trig
  N9: Componente1.D11_PWM/MOSI, Componente3.Echo
  N10: Componente1.D12/MISO, Part1.S
  N11: Componente1.D13/SCK, KY-1.signal
  N12: Componente1.D2, DS2.DQ
  N13: Componente1.D3_PWM, Componente2.Trig
  N14: Componente1.D4, S1.2
  N15: Componente1.D5_PWM, Componente2.Echo
  N16: Componente1.D6_PWM, Componente4.Trig
  N17: Componente1.D7, Componente5.TXD
  VCC: Componente2.VCC, Componente3.VCC, Componente4.VCC, Componente5.VCC, Componente6.VCC, J2.3.3V, J2.5V, DS2.VDD, KY-1.C, KY-2.C
  GND: Componente2.GND, Componente3.GND, Componente4.GND, Componente5.GND, Componente6.GND, F2.GND, J2.GND, DS2.GND, DS2.shield
  N18: Componente6.E+, Load_Cell1.wire1
  N19: Componente6.E-, Load_Cell1.wire3
  N20: Componente6.A+, Load_Cell1.wire2
  N21: Componente6.A-, Load_Cell1.wire4
  N22: F2.5V, KY-2.NO
  N23: J1.pin1, KY-4.C
  N24: J1.pin2, KY-3.C
  N25: J2.PWR_OK, KY-4.NO
  N26: J2.5V_STDBY, KY-3.NO
  N27: J2.12V, KY-3.NC, KY-4.NC
  N28: J2.-12V, KY-4.power
  N29: J2.NC, KY-1.ground
  N30: KY-1.NO, U1.VCC

custom parts:
  Load Cell - Red/white/black/green: A rectangle load cell/weighting pressure Sensor with four wires - Red, white, black, green. Normally corresponding with E+, E-, A+, A- respectively.
  KY-006 Passive Buzzer Module: Passive Piezoelectric Buzzer Module Keyes KY-006, it can produce a range of sound tones depending on the input frequency.
  Fan - Ventilador: Ventilador de 2 pines, se encuentra comunmente en computadoras de escritorio
  Keyes Relay: The Keyes 5V relay module is suitable for SCM development, home appliance control. It uses a 5V~12V TIL control signal which can control DC / AC signal.
  WS2812 RGB LED matrix 1x8: WS2812 matrix 1x8
